# Fritzing sketch 2HP Eurorack Panel Expander (saved by Fritzing 0.9.3b)
circuit board: 0.98cm x 12.7cm
breadboards: 1

parts:
  J1 = double row female pin header, 14 pins [form="♀ (female)"]
  Pad1 = Pad [width=6 height=9.0311111111111106 connect=center]
  Pad2 = Pad [width=6 height=9.0311111111111106 connect=center]
  Pad3 = Pad [width=6 height=9.0311111111111106 connect=center]
  PJ1 = thonkiconn [package="PG203J [THT]"]

nets:
  N1: J1.pin2, PJ1.ground
  N2: J1.pin3, PJ1.signal
  N3: J1.pin4, Pad1.pad
  N4: J1.pin9, Pad3.pad
  N5: J1.pin11, Pad2.pad

notes:
  K_

custom parts:
  thonkiconn: mono switched Jack 3.5mm
