# Fritzing sketch DIN MIDI Expander (saved by Fritzing 0.9.3b)
circuit board: 8.46667cm x 5.64444cm
breadboards: 1

parts:
  J1 = double row female pin header, 14 pins [form="♀ (female)"]
  Rx_on_Teensy_D26 = female pin header, 2 pins [form="♀ (female)"]
  Tx_on_Teensy_D31 = female pin header, 2 pins [form="♀ (female)"]

nets:
  N1: J1.pin6, Rx_on_Teensy_D26.pin1
  N2: J1.pin10, Tx_on_Teensy_D31.pin1
